// Logisim project Final-Circuit.circ as structural Verilog: 5 circuits, main circuit main
module main (
  output [3:0] out_1,
  output [7:0] e
);

  wire and_1_out, and_2_out, and_4_out, and_5_out, and_6_out, and_7_out, clock_1_out, d_ff_2_qn, d_ff_3_qn,
       not_1_out, not_2_out, not_3_out, not_4_out, or_1_out, or_2_out, xor_1_out;
  wire [5:0] or_3_out;

  and and_1 (and_1_out, d_ff_2_qn, out_1[0]);
  or or_1 (or_1_out, and_2_out, out_1[3]);
  and and_2 (and_2_out, d_ff_3_qn, d_ff_2_qn);
  or or_2 (or_2_out, and_2_out, and_1_out);
  xor xor_1 (xor_1_out, out_1[3], out_1[2]);
  Clock clock_1 (.out(clock_1_out));
  D_Flip_Flop d_ff_1 (.clk(clock_1_out), .D(or_1_out), .Q(out_1[0]));  // open: Qn, preset, en, reset
  D_Flip_Flop d_ff_2 (.clk(clock_1_out), .D(or_2_out), .Q(out_1[1]), .Qn(d_ff_2_qn));  // open: preset, en, reset
  D_Flip_Flop d_ff_3 (.clk(clock_1_out), .D(out_1[1]), .Q(out_1[2]), .Qn(d_ff_3_qn));  // open: preset, en, reset
  D_Flip_Flop d_ff_4 (.clk(clock_1_out), .D(xor_1_out), .Q(out_1[3]));  // open: Qn, preset, en, reset
  not not_1 (not_1_out, out_1[3]);
  not not_2 (not_2_out, out_1[1]);
  not not_3 (not_3_out, out_1[2]);
  not not_4 (not_4_out, out_1[0]);
  and and_3 (or_3_out[3], not_1_out, not_3_out, out_1[1], out_1[0]);
  and and_4 (and_4_out, out_1[3], not_3_out, out_1[1], out_1[0]);
  and and_5 (and_5_out, out_1[3], out_1[2], not_2_out, out_1[0]);
  and and_6 (and_6_out, not_1_out, out_1[2], not_2_out, not_4_out);
  and and_7 (and_7_out, out_1[3], not_3_out, not_2_out, not_4_out);
  or or_3 (or_3_out[0], or_3_out[3], and_4_out);
  or or_4 (or_3_out[2], or_3_out[3], and_6_out, and_7_out, and_4_out, and_5_out);
  or or_5 (or_3_out[4], and_4_out, and_5_out);
  or or_6 (or_3_out[5], or_3_out[3], and_5_out, and_4_out);
  D_Flip_Flop d_ff_5 (.clk(clock_1_out), .D(or_3_out[0]), .Q(e[0]));  // open: Qn, preset, en, reset
  D_Flip_Flop d_ff_6 (.clk(clock_1_out), .D(or_3_out[2]), .Q(e[1]));  // open: Qn, preset, en, reset
  D_Flip_Flop d_ff_7 (.clk(clock_1_out), .D(or_3_out[2]), .Q(e[2]));  // open: Qn, preset, en, reset
  D_Flip_Flop d_ff_8 (.clk(clock_1_out), .D(or_3_out[3]), .Q(e[3]));  // open: Qn, preset, en, reset
  D_Flip_Flop d_ff_9 (.clk(clock_1_out), .Q(e[4]));  // open: D, Qn, preset, en, reset
  D_Flip_Flop d_ff_10 (.clk(clock_1_out), .D(or_3_out[4]), .Q(e[5]));  // open: Qn, preset, en, reset
  D_Flip_Flop d_ff_11 (.clk(clock_1_out), .D(or_3_out[5]), .Q(e[6]));  // open: Qn, preset, en, reset
  D_Flip_Flop d_ff_12 (.clk(clock_1_out), .Q(e[7]));  // open: D, Qn, preset, en, reset
  _7_Segment_Display u_7_segment_display_1 (.g(e[6]), .f(e[5]), .a(e[0]), .b(e[1]), .d(e[3]), .c(e[2]));  // open: e, dp

  // Notes on the sheet:
  //   A
  //   B
  //   C
  //   Figure: Sequential and Combinational Circuit using D flip-flop and register
  //   D
  //   d
  //   a
  //   b
  //   c
  //   f
  //   g
  //   c
  //   a
  //   g
  //   b
  //   f
  //   d
endmodule

module Counter_with_D_flip_flop (
  output [3:0] out_1
);

  wire and_1_out, and_2_out, clock_1_out, d_ff_2_qn, d_ff_3_qn, or_1_out, or_2_out, xor_1_out;

  and and_1 (and_1_out, d_ff_2_qn, out_1[0]);
  and and_2 (and_2_out, d_ff_3_qn, d_ff_2_qn);
  or or_1 (or_1_out, and_2_out, out_1[3]);
  or or_2 (or_2_out, and_2_out, and_1_out);
  xor xor_1 (xor_1_out, out_1[3], out_1[2]);
  Clock clock_1 (.out(clock_1_out));
  D_Flip_Flop d_ff_1 (.clk(clock_1_out), .D(or_1_out), .Q(out_1[0]));  // open: Qn, preset, en, reset
  D_Flip_Flop d_ff_2 (.clk(clock_1_out), .D(or_2_out), .Q(out_1[1]), .Qn(d_ff_2_qn));  // open: preset, en, reset
  D_Flip_Flop d_ff_3 (.clk(clock_1_out), .D(out_1[1]), .Q(out_1[2]), .Qn(d_ff_3_qn));  // open: preset, en, reset
  D_Flip_Flop d_ff_4 (.clk(clock_1_out), .D(xor_1_out), .Q(out_1[3]));  // open: Qn, preset, en, reset

  // Notes on the sheet:
  //   Figure: Counter with D flip-flop
endmodule

module Combinational_circuit (
  input  A,
  input  B,
  input  C,
  input  D
);

  wire and_1_out, and_2_out, and_3_out, and_4_out, and_5_out, not_1_out, not_2_out, not_3_out, not_4_out,
       or_1_out, or_2_out, or_3_out, or_4_out;

  not not_1 (not_1_out, A);
  not not_2 (not_2_out, B);
  not not_3 (not_3_out, C);
  not not_4 (not_4_out, D);
  and and_1 (and_1_out, not_1_out, not_2_out, C, D);
  and and_2 (and_2_out, A, not_2_out, C, D);
  and and_3 (and_3_out, A, B, not_3_out, D);
  and and_4 (and_4_out, not_1_out, B, not_3_out, not_4_out);
  and and_5 (and_5_out, A, not_2_out, not_3_out, not_4_out);
  or or_1 (or_1_out, and_1_out, and_2_out);
  or or_2 (or_2_out, and_1_out, and_4_out, and_5_out, and_2_out, and_3_out);
  or or_3 (or_3_out, and_2_out, and_3_out);
  or or_4 (or_4_out, and_1_out, and_3_out, and_2_out);
  _7_Segment_Display u_7_segment_display_1 (
    .g(or_4_out), .f(or_3_out), .a(or_1_out), .b(or_2_out), .d(and_1_out), .c(or_2_out));  // open: e, dp

  // Notes on the sheet:
  //   Figure: Combinational Circuit
  //   a
  //   d
  //   f
  //   g
  //   b
  //   c
endmodule

module Register_with_D_flip_flop (
  input  [7:0] in_1,
  output [7:0] out_2
);

  wire clock_1_out;

  Clock clock_1 (.out(clock_1_out));
  D_Flip_Flop d_ff_1 (.clk(clock_1_out), .D(in_1[0]), .Q(out_2[0]));  // open: Qn, preset, en, reset
  D_Flip_Flop d_ff_2 (.clk(clock_1_out), .D(in_1[1]), .Q(out_2[1]));  // open: Qn, preset, en, reset
  D_Flip_Flop d_ff_3 (.clk(clock_1_out), .D(in_1[2]), .Q(out_2[2]));  // open: Qn, preset, en, reset
  D_Flip_Flop d_ff_4 (.clk(clock_1_out), .D(in_1[3]), .Q(out_2[3]));  // open: Qn, preset, en, reset
  D_Flip_Flop d_ff_5 (.clk(clock_1_out), .D(in_1[4]), .Q(out_2[4]));  // open: Qn, preset, en, reset
  D_Flip_Flop d_ff_6 (.clk(clock_1_out), .D(in_1[5]), .Q(out_2[5]));  // open: Qn, preset, en, reset
  D_Flip_Flop d_ff_7 (.clk(clock_1_out), .Q(out_2[6]));  // open: D, Qn, preset, en, reset
  D_Flip_Flop d_ff_8 (.clk(clock_1_out), .Q(out_2[7]));  // open: D, Qn, preset, en, reset

  // Notes on the sheet:
  //   8 bit parallel register with D flip-flop
endmodule

module counter_and_co_circuit (
  output [3:0] out_1
);

  wire and_1_out, and_2_out, and_3_out, and_4_out, and_5_out, and_6_out, and_7_out, clock_1_out, d_ff_2_qn,
       d_ff_3_qn, not_1_out, not_2_out, not_3_out, not_4_out, or_1_out, or_2_out, or_3_out, or_4_out,
       or_5_out, or_6_out, xor_1_out;

  and and_1 (and_1_out, d_ff_2_qn, out_1[0]);
  or or_1 (or_1_out, and_2_out, out_1[3]);
  and and_2 (and_2_out, d_ff_3_qn, d_ff_2_qn);
  or or_2 (or_2_out, and_2_out, and_1_out);
  xor xor_1 (xor_1_out, out_1[3], out_1[2]);
  Clock clock_1 (.out(clock_1_out));
  D_Flip_Flop d_ff_1 (.clk(clock_1_out), .D(or_1_out), .Q(out_1[0]));  // open: Qn, preset, en, reset
  D_Flip_Flop d_ff_2 (.clk(clock_1_out), .D(or_2_out), .Q(out_1[1]), .Qn(d_ff_2_qn));  // open: preset, en, reset
  D_Flip_Flop d_ff_3 (.clk(clock_1_out), .D(out_1[1]), .Q(out_1[2]), .Qn(d_ff_3_qn));  // open: preset, en, reset
  D_Flip_Flop d_ff_4 (.clk(clock_1_out), .D(xor_1_out), .Q(out_1[3]));  // open: Qn, preset, en, reset
  not not_1 (not_1_out, out_1[3]);
  not not_2 (not_2_out, out_1[2]);
  not not_3 (not_3_out, out_1[1]);
  not not_4 (not_4_out, out_1[0]);
  and and_3 (and_3_out, not_1_out, not_2_out, out_1[1], out_1[0]);
  and and_4 (and_4_out, out_1[3], not_2_out, out_1[1], out_1[0]);
  and and_5 (and_5_out, out_1[3], out_1[2], not_3_out, out_1[0]);
  and and_6 (and_6_out, not_1_out, out_1[2], not_3_out, not_4_out);
  and and_7 (and_7_out, out_1[3], not_2_out, not_3_out, not_4_out);
  or or_3 (or_3_out, and_3_out, and_4_out);
  or or_4 (or_4_out, and_3_out, and_6_out, and_7_out, and_4_out, and_5_out);
  or or_5 (or_5_out, and_4_out, and_5_out);
  or or_6 (or_6_out, and_3_out, and_5_out, and_4_out);
  _7_Segment_Display u_7_segment_display_1 (
    .g(or_6_out), .f(or_5_out), .a(or_3_out), .b(or_4_out), .d(and_3_out), .c(or_4_out));  // open: e, dp

  // Notes on the sheet:
  //   Fugure: Sequential Circuit
  //   A
  //   B
  //   C
  //   D
  //   d
  //   a
  //   b
  //   f
  //   g
  //   c
endmodule
